# Fritzing sketch charger (saved by Fritzing 0.7.0b)
breadboards: 1

parts:
  5k = 220 Ω Resistor [package=THT]
  Arduino2 = Arduino
  1k = 220 Ω Resistor [package=THT]
  T1 = LM35 Temperature Sensor [package="TO92 [THT]"]
  Q4 = Basic FET P-Channel [package="TO220 [THT]"]
  VCC1 = Battery block 9V
  220k = 220 Ω Resistor [package=THT]
  80k = 220 Ω Resistor [package=THT]

nets:
  N1: 5k.Pin_0, Q4.source
  N2: 5k.Pin_1, Arduino2.D3, T1.GND, Q4.gate
  N3: Arduino2.D6, 1k.Pin_1
  N4: Arduino2.GND, T1.+Vs, VCC1.-
  N5: Arduino2.A5, 220k.Pin_0, 80k.Pin_1
  N6: 1k.Pin_0, T1.Vout
  N7: Q4.drain, VCC1.+, 220k.Pin_1

notes:
  output of dc/dc converter
